# Fritzing sketch AritechArduinoProtoShield (saved by Fritzing 0.9.1b)

parts:
  Part2 = Adafruit Proto Shield R3 [part_number="Adafruit #2077"]
  Q1 = NPN-Transistor [package="TO92 [THT]"]
  Q2 = NPN-Transistor [package="TO92 [THT]"]
  R1 = Resistor Mini [tolerance=±5% resistance=4.7k package=THT]
  R4 = Resistor Mini [tolerance=±5% resistance=4.7k package=THT]
  R5 = Resistor Mini [tolerance=±5% resistance=4.7k package=THT]
  R6 = Resistor Mini [tolerance=±5% resistance=4.7k package=THT]
  R7 = Resistor Mini [tolerance=±5% resistance=22k package=THT]
  R8 = Resistor Mini [tolerance=±5% resistance=10k package=THT]
  JACK1 = 2.1mm Barrel Jack with Terminal Block

nets:
  N1: Part2.1#0, Part2.P$5#1, Part2.P$6#2, Part2.1#129, Part2.P$5#130, Part2.P$6#131, Part2.N$90, R4.Pin_1, R8.Pin_1, JACK1.POS
  N2: Part2.GND, Part2.1#193, Part2.P$5#194, Part2.N$16, Part2.P$5#197, Part2.N$101, Q1.E, Q2.E, JACK1.NEG
  N3: Part2.D0, Part2.1#163, Part2.P$5#164, R6.Pin_1
  N4: Part2.D1, Part2.P$5#127, Part2.P$6#128, R1.Pin_1
  N5: Part2.1#132, Part2.P$5#133, Part2.N$99, R5.Pin_1
  N6: Part2.N$115, Part2.P$5#161, Part2.P$6#162, Part2.1#166, Part2.P$6#168, Q2.B, R6.Pin_0, R8.Pin_0
  N7: Part2.1#172, Part2.P$5#173, Q2.C, R7.Pin_0
  N8: Part2.1#180, Part2.P$5#181, Q1.C, R1.Pin_0
  N9: Part2.1#183, Part2.P$6#185, Part2.N$15, Part2.P$5#200, Part2.P$6#201, Q1.B, R4.Pin_0, R5.Pin_0
  N10: Part2.1#202, Part2.P$5#203, Part2.N$269, R7.Pin_1

custom parts:
  Adafruit Proto Shield R3: This prototyping shield is the best out there (well, we think so, at least), and now is even better with Version R3 - updated for the most compatibility with just about all the Arduinos! It works with UNO, Mega, Leonardo, NG, Diecimila, Duemilanove, and compatible Arduinos. Yun's and Arduino Ethernets have a chunky Ethernet jack that gets in the way of stacking, you can use the stacking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
  Resistor Mini: A generic resistor (0.25W)
