# Fritzing sketch AritechESP32ProtoShield (saved by Fritzing 0.9.1b)

parts:
  Part2 = Adafruit Proto Shield R3 [part_number="Adafruit #2077"]
  R1 = Resistor Mini [tolerance=±5% resistance=4.7k package=THT]
  R4 = Resistor Mini [tolerance=±5% resistance=4.7k package=THT]
  R5 = Resistor Mini [tolerance=±5% resistance=1.5k package=THT]
  R6 = Resistor Mini [tolerance=±5% resistance=4.7k package=THT]
  R7 = Resistor Mini [tolerance=±5% resistance=22k package=THT]
  R8 = Resistor Mini [tolerance=±5% resistance=15k package=THT]
  JACK1 = 2.1mm Barrel Jack with Terminal Block
  Q3 = NPN-Transistor [package="TO92 [THT]"]
  Q4 = NPN-Transistor [package="TO92 [THT]"]
  C1 = Electrolytic Capacitor [capacitance=1µF package="100 mil [THT, electrolytic]"]
  R9 = Resistor Mini [tolerance=±5% resistance=220 package=THT]
  R10 = Resistor Mini [tolerance=±5% resistance=220 package=THT]

nets:
  N1: Part2.1#0, Part2.P$5#1, Part2.P$6#2, Part2.1#129, Part2.P$5#130, Part2.P$6#131, Part2.N$90, R4.Pin_1, R8.Pin_1, JACK1.POS
  N2: Part2.GND, Part2.1#163, Part2.P$5#164, Part2.1#193, Part2.P$5#194, Part2.N$16, Part2.P$5#197, Part2.P$6#198, Part2.N$101, Part2.N$138, Part2.N$173, R6.Pin_1, JACK1.NEG, Q3.E, Q4.E, C1.-, R9.Pin_1, R10.Pin_1
  N3: Part2.D3, R10.Pin_0
  N4: Part2.D4, R9.Pin_0
  N5: Part2.D5, Part2.P$5#170, Part2.P$6#171, R1.Pin_1
  N6: Part2.D6, Part2.N$115, Part2.P$5#161, Part2.P$6#162, Part2.1#166, Part2.P$5#167, Part2.P$6#168, R6.Pin_0, R8.Pin_0, Q3.C
  N7: Part2.1#132, Part2.P$5#133, Part2.N$99, R5.Pin_1
  N8: Part2.AREF, C1.+
  N9: Part2.1#172, Part2.P$5#173, R7.Pin_0, Q3.B
  N10: Part2.P$5#181, Part2.P$6#182, R1.Pin_0, Q4.B
  N11: Part2.1#183, Part2.P$6#185, Part2.N$15, Part2.P$5#200, Part2.P$6#201, R4.Pin_0, R5.Pin_0, Q4.C
  N12: Part2.1#202, Part2.P$5#203, Part2.N$269, R7.Pin_1

custom parts:
  Adafruit Proto Shield R3: This prototyping shield is the best out there (well, we think so, at least), and now is even better with Version R3 - updated for the most compatibility with just about all the Arduinos! It works with UNO, Mega, Leonardo, NG, Diecimila, Duemilanove, and compatible Arduinos. Yun's and Arduino Ethernets have a chunky Ethernet jack that gets in the way of stacking, you can use the stacking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
  Resistor Mini: A generic resistor (0.25W)
