# Fritzing sketch HkcESP32ProtoShield (saved by Fritzing 0.9.1b)

parts:
  Part2 = Adafruit Proto Shield R3 [part_number="Adafruit #2077"]
  R4 = Resistor Mini [tolerance=±5% resistance=560 package=THT]
  R7 = Resistor Mini [tolerance=±5% resistance=4.7k package=THT]
  JACK1 = 2.1mm Barrel Jack with Terminal Block
  Q3 = NPN-Transistor [package="TO92 [THT]"]
  Q4 = NPN-Transistor [package="TO92 [THT]"]
  R9 = Resistor Mini [tolerance=±5% resistance=220 package=THT]
  R10 = Resistor Mini [tolerance=±5% resistance=220 package=THT]
  Q5 = NPN-Transistor [package="TO92 [THT]"]
  R11 = Resistor Mini [tolerance=±5% resistance=4.7k package=THT]
  R12 = Resistor Mini [tolerance=±5% resistance=4.7k package=THT]

nets:
  N1: Part2.GND, Part2.1#193, Part2.P$5#194, Part2.N$35, Part2.N$172, Part2.N$210, JACK1.NEG, Q3.E, Q5.E
  N2: Part2.D3, R10.Pin_0
  N3: Part2.D4, R9.Pin_0
  N4: Part2.D6, Part2.P$5#167, Part2.P$6#168, R11.Pin_0
  N5: Part2.D7, Part2.P$5#161, Q3.C
  N6: Part2.1#123, Part2.P$5#124, Part2.1#132, Part2.P$5#133, Part2.1#183, Part2.P$5#184, Part2.N$46, Part2.N$215, JACK1.POS, Q4.C, R12.Pin_1
  N7: Part2.P$5#127, Part2.P$6#128, Part2.P$5#203, Part2.P$6#204, Part2.N$18, R4.Pin_1, R7.Pin_1
  N8: Part2.1#172, Part2.P$5#173, R7.Pin_0, Q3.B
  N9: Part2.P$5#177, Part2.P$6#178, Q5.B, R11.Pin_1
  N10: Part2.1#180, Part2.P$5#181, R4.Pin_0, Q4.E
  N11: Part2.N$16, Part2.P$5#197, Part2.P$6#198, Part2.P$5#200, Part2.P$6#201, Q4.B, Q5.C, R12.Pin_0
  N12: Part2.N$139, R9.Pin_1
  N13: Part2.N$174, R10.Pin_1

custom parts:
  Adafruit Proto Shield R3: This prototyping shield is the best out there (well, we think so, at least), and now is even better with Version R3 - updated for the most compatibility with just about all the Arduinos! It works with UNO, Mega, Leonardo, NG, Diecimila, Duemilanove, and compatible Arduinos. Yun's and Arduino Ethernets have a chunky Ethernet jack that gets in the way of stacking, you can use the stacking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
  Resistor Mini: A generic resistor (0.25W)
